# Fritzing sketch watering-robot (saved by Fritzing 0.8.7b)
breadboards: 1

parts:
  Raspberry_Pi_A1 = Raspberry Pi A
  パーツ1 = Arduino Uno (Rev3) - ICSP

nets:
  5V: Raspberry_Pi_A1.5V, パーツ1.5V
  GND: Raspberry_Pi_A1.GND, パーツ1.GND
